// Logisim project alu2.circ as structural Verilog: 3 circuits, main circuit main
module main (
  input  [3:0] FunSel,
  input  [7:0] A,
  input  [7:0] B,
  input  in_4,
  input  in_5,
  input  in_6,
  output [7:0] Out,
  output [3:0] ZNCO
);

  wire and_2_out, arithmetic_unit_1_carry_output, clock_1_out, shifter_1_carryout;
  wire [3:0] arithmetic_unit_1_overflow;
  wire [7:0] and_1_out, arithmetic_unit_1_out, not_1_out, not_2_out, or_1_out, shifter_1_out, xor_1_out;

  arithmetic_unit arithmetic_unit_1 (
    .FunSel(FunSel[1:0]), .A(A), .B(B), .Carry(in_4), .Out(arithmetic_unit_1_out),
    .Carry_output(arithmetic_unit_1_carry_output), .Overflow(arithmetic_unit_1_overflow[0]));
  assign and_1_out = A & B;  // AND_Gate and_1, 8 bits wide
  assign or_1_out = A | B;  // OR_Gate or_1, 8 bits wide
  assign xor_1_out = A ^ B;  // XOR_Gate xor_1, 8 bits wide
  shifter shifter_1 (
    .Out(shifter_1_out), .CarryOut(shifter_1_carryout), .Funsel(FunSel[2:0]), .A(A), .in_4(in_5),
    .in_3(in_5), .in_5(in_5));
  or or_2 (arithmetic_unit_1_overflow[1], arithmetic_unit_1_carry_output, shifter_1_carryout);
  assign not_1_out = ~A;  // NOT_Gate not_1, 8 bits wide
  assign not_2_out = ~B;  // NOT_Gate not_2, 8 bits wide
  Multiplexer #(.select(4), .width(8), .enable("false")) multiplexer_1 (
    .in0(A), .in1(B), .in2(not_1_out), .in3(not_2_out), .in4(arithmetic_unit_1_out),
    .in5(arithmetic_unit_1_out), .in6(arithmetic_unit_1_out), .in7(and_1_out), .in8(or_1_out),
    .in9(xor_1_out), .in10(shifter_1_out), .in11(shifter_1_out), .in12(shifter_1_out), .in13(shifter_1_out),
    .in14(shifter_1_out), .in15(shifter_1_out), .out(Out), .sel(FunSel));
  and and_2 (and_2_out, Out[0], Out[1], Out[2], Out[3], Out[4], Out[5], Out[6], Out[7]);
  not not_3 (arithmetic_unit_1_overflow[3], and_2_out);
  Clock clock_1 (.out(clock_1_out));
  Register #(.width(4)) register_1 (
    .D({arithmetic_unit_1_overflow[3], Out[7], arithmetic_unit_1_overflow[1:0]}), .en(in_6), .Q(ZNCO),
    .clk(clock_1_out));  // open: clr
endmodule

// Arithmetic Unit
module arithmetic_unit (
  input  Carry,
  input  [1:0] FunSel,
  input  [7:0] A,
  input  [7:0] B,
  output [7:0] Out,
  output Carry_output,
  output Overflow
);

  wire and_1_out, not_1_out, xor_1_out, xor_2_out;
  wire [7:0] adder_1_out, subtractor_1_out;

  and and_1 (and_1_out, Carry, FunSel[0]);
  Adder adder_1 (.a(A), .b(B), .out(adder_1_out), .cin(and_1_out), .cout(Carry_output));
  Subtractor subtractor_1 (.a(A), .b(B), .out(subtractor_1_out));  // open: bin, bout
  Multiplexer #(.select(2), .width(8), .enable("false")) multiplexer_1 (
    .in0(adder_1_out), .in1(adder_1_out), .in2(subtractor_1_out), .in3(subtractor_1_out), .out(Out),
    .sel(FunSel));
  not not_1 (not_1_out, Out[7]);
  xor xor_1 (xor_1_out, B[7], A[7]);
  xor xor_2 (xor_2_out, not_1_out, xor_1_out);
  not not_2 (Overflow, xor_2_out);
endmodule

module shifter (
  input  [2:0] Funsel,
  input  [7:0] A,
  input  in_3,
  input  in_4,
  input  in_5,
  output [7:0] Out,
  output CarryOut
);

  Multiplexer #(.select(3), .width(8), .enable("false")) multiplexer_1 (
    .in0({A[6:0], in_3}), .in1({A[6:0], in_3}), .in2({A[6:0], in_3}), .in3({in_4, A[7:1]}),
    .in4({A[6:0], in_5}), .in5({{2{A[7]}}, A[6:1]}), .in6({A[6:0], A[7]}), .in7({A[0], A[7:1]}), .out(Out),
    .sel(Funsel));
  Multiplexer #(.select(3), .enable("false")) multiplexer_2 (
    .in0(A[7]), .in1(A[7]), .in2(A[7]), .in3(A[0]), .in4(A[7]), .in5(A[7]), .in6(A[7]), .in7(A[0]),
    .out(CarryOut), .sel(Funsel));

  // Notes on the sheet:
  //   Carry
endmodule
